// Logisim project ula.circ as structural Verilog: 6 circuits, main circuit somadorDe2bits
module somadorDe2bits (
  input  A0,
  input  B0,
  input  A1,
  input  B1,
  output soma0,
  output carry1,
  output soma1,
  output carry2
);

  wire and2_out, and3_out, xor2_out;

  xor xor1 (soma0, A0, B0);
  and AND1 (carry1, A0, B0);
  xor xor2 (xor2_out, A1, B1);
  and and2 (and2_out, A1, B1);
  xor xor3 (soma1, xor2_out, carry1);
  and and3 (and3_out, carry1, xor2_out);
  or or2 (carry2, and2_out, and3_out);
endmodule

module subtratorDe2bits (
  input  A0,
  input  B0,
  input  A1,
  input  B1,
  output diferenca0,
  output borrow0,
  output diferenca1,
  output borrowOut
);

  wire and2_out, and3_out, not_1_out, xor3_out;

  not not_1 (not_1_out, A0);
  and and2 (and2_out, A1, B1);
  xor xor1 (diferenca0, A0, B0);
  and and1 (borrow0, not_1_out, B0);
  xor xor3 (xor3_out, A1, B1);
  xor xor4 (diferenca1, xor3_out, borrow0);
  and and3 (and3_out, xor3_out, borrow0);
  or or_1 (borrowOut, and2_out, and3_out);
endmodule

module multiplicadorDe2bits (
  input  A0,
  input  B0,
  input  A1,
  input  B1,
  output Y0,
  output Y1,
  output Carry1,
  output Y2,
  output Y3
);

  wire AND2_out, AND3_out, and4_out, and5_out, and7_out, AND8_out;

  and and4 (and4_out, A1, B0);
  and and5 (and5_out, A0, B1);
  and and7 (and7_out, A1, B1);
  and AND8 (AND8_out, A1, B1);
  and AND1 (Y0, A0, B0);
  and AND2 (AND2_out, A1, B0);
  and AND3 (AND3_out, A0, B1);
  and and6 (Carry1, and4_out, and5_out);
  and and9 (Y3, Carry1, AND8_out);
  xor xor1 (Y1, AND2_out, AND3_out);
  xor xor2 (Y2, Carry1, and7_out);
endmodule

module divisorDe2bits (
  input  A0,
  input  B0,
  input  A1,
  input  B1,
  output Y1,
  output ERRO,
  output Y0
);

  wire and_3_out, and_4_out, and_5_out, and_6_out, not_1_out, not_2_out, or1_out;

  not not_1 (not_1_out, B0);
  not not_2 (not_2_out, B1);
  and and_1 (Y1, not_2_out, B0, A1);
  and and_2 (ERRO, not_1_out, not_2_out);
  and and_3 (and_3_out, not_1_out, B1, A1);
  and and_4 (and_4_out, B0, not_2_out, A0);
  and and_5 (and_5_out, B0, B1, A1, A0);
  and and_6 (and_6_out, and_5_out, A1);
  or or1 (or1_out, and_3_out, and_4_out);
  or or2 (Y0, or1_out, and_6_out);
endmodule

module MULTIPLEXADOR4X1 (
  input  In0_Soma,
  input  In1_Sub,
  input  In2_Mult,
  input  In3_Div,
  input  S1,
  input  S0,
  output SAIDA
);

  wire DIV_out, MAIS_out, MULT_out, not_1_out, not_2_out, OR1_out, OR2_out, SUB_out;

  not not_1 (not_1_out, S1);
  not not_2 (not_2_out, S0);
  and MAIS (MAIS_out, In0_Soma, not_1_out, not_2_out);
  and SUB (SUB_out, In1_Sub, not_1_out, S0);
  and MULT (MULT_out, In2_Mult, S1, not_2_out);
  and DIV (DIV_out, In3_Div, S1, S0);
  or OR1 (OR1_out, MAIS_out, SUB_out);
  or OR2 (OR2_out, MULT_out, DIV_out);
  or OR3 (SAIDA, OR1_out, OR2_out);
endmodule

module ULA (
  input  S1,
  input  S0,
  input  A0,
  input  B0,
  input  A1,
  input  B1,
  output Y1,
  output Y0
);

  wire divisorde2bits_1_erro, divisorde2bits_1_y0, divisorde2bits_1_y1, multiplicadorde2bits_1_y0,
       multiplicadorde2bits_1_y1, somadorde2bits_1_p6, somadorde2bits_1_p7, subtratorde2bits_1_borrow0,
       subtratorde2bits_1_borrowout, subtratorde2bits_1_diferenca0, subtratorde2bits_1_diferenca1;

  // somadorDe2bits somadorde2bits_1: pin names not known; wires that end beside it: A0, B0, A1, B1, 1'b0, somadorde2bits_1_p6, somadorde2bits_1_p7
  subtratorDe2bits subtratorde2bits_1 (
    .A0(A0), .B0(B0), .A1(A1), .B1(B1), .diferenca0(subtratorde2bits_1_diferenca0),
    .borrow0(subtratorde2bits_1_borrow0), .diferenca1(subtratorde2bits_1_diferenca1),
    .borrowOut(subtratorde2bits_1_borrowout));
  LED led_1 (.in(subtratorde2bits_1_borrow0));
  LED led_2 (.in(subtratorde2bits_1_borrowout));
  multiplicadorDe2bits multiplicadorde2bits_1 (
    .A0(A0), .B0(B0), .A1(A1), .B1(B1), .Y0(multiplicadorde2bits_1_y0), .Y1(multiplicadorde2bits_1_y1));  // open: Carry1, Y2, Y3
  divisorDe2bits divisorde2bits_1 (
    .A0(A0), .B0(B0), .A1(A1), .B1(B1), .Y1(divisorde2bits_1_y1), .ERRO(divisorde2bits_1_erro),
    .Y0(divisorde2bits_1_y0));
  LED led_3 (.in(divisorde2bits_1_erro));
  MULTIPLEXADOR4X1 multiplexador4x1_1 (
    .In0_Soma(somadorde2bits_1_p7), .In1_Sub(subtratorde2bits_1_diferenca1),
    .In2_Mult(multiplicadorde2bits_1_y1), .In3_Div(divisorde2bits_1_y1), .S1(S1), .S0(S0), .SAIDA(Y1));
  MULTIPLEXADOR4X1 multiplexador4x1_2 (
    .In0_Soma(somadorde2bits_1_p6), .In1_Sub(subtratorde2bits_1_diferenca0),
    .In2_Mult(multiplicadorde2bits_1_y0), .In3_Div(divisorde2bits_1_y0), .S1(S1), .S0(S0), .SAIDA(Y0));
endmodule
